# Fritzing sketch WMS-REF (saved by Fritzing 0.9.9b)
circuit board: 12.3169cm x 4.66718cm
breadboards: 1

parts:
  Part1 = Soil Moisture Sensor
  LED1 = smd LED [color="Red (633nm)" package="0603 [SMD]"]
  WeMos_D1_Mini1 = WeMos D1 Mini
  SG1 = Buzzer 12mm [package=buzzer-12mm-ns-kit]
  LCM1602_IIC1 = LCM1602 IIC [part_number="LCM1602 IIC" chip_label="LCM1602 IIC" package="DIP (Dual Inline) [THT]"]
  LCD1 = LCD screen

nets:
  VCC: Part1.VCC, WeMos_D1_Mini1.3V3
  GND: Part1.GND, WeMos_D1_Mini1.G, LCM1602_IIC1.GND
  N1: Part1.SIG, WeMos_D1_Mini1.A0
  N2: LED1.cathode, SG1.1
  N3: LED1.anode, WeMos_D1_Mini1.D6
  5V: WeMos_D1_Mini1.5V, LCM1602_IIC1.VCC
  N4: WeMos_D1_Mini1.D1, LCM1602_IIC1.SCL
  N5: WeMos_D1_Mini1.D2, LCM1602_IIC1.SDA
  N6: WeMos_D1_Mini1.D5, SG1.2
  VSS: LCM1602_IIC1.VSS, LCD1.VSS
  VDD: LCM1602_IIC1.VDD, LCD1.VDD
  N7: LCM1602_IIC1.V0, LCD1.V0
  N8: LCM1602_IIC1.RS, LCD1.RS
  N9: LCM1602_IIC1.RW, LCD1.R/W
  N10: LCM1602_IIC1.E, LCD1.E
  N11: LCM1602_IIC1.D0, LCD1.DB0
  N12: LCM1602_IIC1.D1, LCD1.DB1
  N13: LCM1602_IIC1.D2, LCD1.DB2
  N14: LCM1602_IIC1.D3, LCD1.DB3
  N15: LCM1602_IIC1.D4, LCD1.DB4
  N16: LCM1602_IIC1.D5, LCD1.DB5
  N17: LCM1602_IIC1.D6, LCD1.DB6
  N18: LCM1602_IIC1.D7, LCD1.DB7
  N19: LCM1602_IIC1.A, LCD1.LED+
  N20: LCM1602_IIC1.K, LCD1.LED-

custom parts:
  LCM1602 IIC: I2C-Module to use a 1602 or 2004 LCD on with the wire.h libory Serial LCD Modul
